# Fritzing sketch Split-flap_595 (saved by Fritzing 0.9.3b)
breadboards: 1

parts:
  Part1 = Arduino Uno (Rev3)
  IC1 = SHIFT REGISTER [package=dil16]
  R1 = Resistor [tolerance=±5% resistance=10k package=THT]
  Q1 = PHOTOTRANSISTOR REFLECTIVE OBJECT SENSOR [package=qrb1114-side]
  IC3 = ULN2003A [package="DIP16 [THT]"]
  J1 = Power Jack [package=power_jack_slot]
  M1 = Stepper Motor - Unipolar
  R2 = Resistor [tolerance=±5% resistance=10k package=THT]
  R3 = Resistor [tolerance=±5% resistance=470 package=THT]
  R4 = Resistor [tolerance=±5% resistance=0 package=THT]
  C1 = Ceramic Capacitor [capacitance=100nF package="100 mil [THT, multilayer]"]

nets (from the schematic view):
  N1: Part1.D10_PWM/SS, IC1.G
  N2: Part1.D11_PWM/MOSI, IC1.SER
  N3: Part1.D12/MISO, R4.Pin_0
  N4: Part1.D13/SCK, IC1.SCK, IC1.RCK
  Vlogic: Part1.5V, IC1.SCL, IC1.VCC, R2.Pin_0, R3.Pin_0, C1.1
  GND: Part1.GND, IC1.GND, Q1.E, Q1.K, IC3.0V, J1.GND, C1.0
  N5: IC1.QB, IC3.In_4
  N6: IC1.QC, IC3.In_3
  N7: IC1.QD, IC3.In_2
  N8: IC1.QE, IC3.In_1
  N9: IC1.QH, R1.Pin_1, R4.Pin_1
  N10: R1.Pin_0, Q1.C, R2.Pin_1
  N11: Q1.A, R3.Pin_1
  Vmotor: IC3.COM_-_Common, J1.PWR, M1.COMMON_1, M1.COMMON_2
  N12: IC3.Out_4, M1.D
  N13: IC3.Out_3, M1.B
  N14: IC3.Out_2, M1.C
  N15: IC3.Out_1, M1.A
